# Fritzing sketch 3ledsversion (saved by Fritzing 0.8.7b)
circuit board: 7cm x 7cm
breadboards: 1

parts:
  R7 = Resistor [tolerance=±5% resistance=22k package=THT]
  R6 = Resistor [tolerance=±5% resistance=1 package=THT]
  R9 = Resistor [tolerance=±5% resistance=1 package=THT]
  Q4 = Basic FET N-Channel [package="TO220 [THT]"]
  R4 = Resistor [tolerance=±5% resistance=22k package=THT]
  R2 = Resistor [tolerance=±5% resistance=1 package=THT]
  R5 = Resistor [tolerance=±5% resistance=1 package=THT]
  Q5 = NPN-Transistor [package="TO92 [THT]"]
  R1 = Resistor [tolerance=±5% resistance=22k package=THT]
  R8 = Resistor [tolerance=±5% resistance=1 package=THT]
  R3 = Resistor [tolerance=±5% resistance=1 package=THT]
  Q2 = Basic FET N-Channel [package="TO220 [THT]"]
  Q1 = NPN-Transistor [package="TO92 [THT]"]
  J1 = screw terminal, 2 pins
  XTAL1 = Crystal [frequency="16 Mhz" package=THT]
  R10 = Resistor [tolerance=±5% resistance=10k package=THT]
  Q3 = NPN-Transistor [package="TO92 [THT]"]
  Atmega328 = atmega328 [package=dip]
  U1 = MAX485 [package=dil08]
  J3 = screw terminal, 4 pins
  Q6 = Basic FET N-Channel [package="TO220 [THT]"]
  J2 = screw terminal, 12 pins
  R11 = Resistor [tolerance=±5% resistance=220 package=THT]
  R12 = Resistor [tolerance=±5% resistance=220 package=THT]
  R13 = Resistor [tolerance=±5% resistance=220 package=THT]
  R14 = Resistor [tolerance=±5% resistance=220 package=THT]
  R16 = Resistor [tolerance=±5% resistance=220 package=THT]
  R15 = Resistor [tolerance=±5% resistance=220 package=THT]
  R17 = Resistor [tolerance=±5% resistance=220 package=THT]
  R19 = Resistor [tolerance=±5% resistance=220 package=THT]
  R18 = Resistor [tolerance=±5% resistance=220 package=THT]

nets:
  N1: R7.Pin_0, Atmega328.D9_(PWM)
  N2: R7.Pin_1, Q5.E, Q6.gate
  N3: R6.Pin_0, R9.Pin_0, R2.Pin_0, R5.Pin_0, Q5.C, R8.Pin_0, R3.Pin_0, Q1.C, J1.pin1, Q3.C, Atmega328.GND, U1.RE, U1.DE
  N4: R6.Pin_1, Q4.source, R5.Pin_1, Q3.B
  N5: R9.Pin_1, Q5.B, R8.Pin_1, Q6.source
  N6: Q4.gate, R4.Pin_1, Q3.E
  N7: Q4.drain, R14.Pin_1, R16.Pin_1, R15.Pin_1
  N8: R4.Pin_0, Atmega328.D10_(PWM)
  N9: R2.Pin_1, R3.Pin_1, Q2.source, Q1.B
  N10: R1.Pin_0, Atmega328.D11_(PWM)
  N11: R1.Pin_1, Q2.gate, Q1.E
  N12: Q2.drain, R17.Pin_1, R19.Pin_1, R18.Pin_1
  N13: J1.pin2, R10.Pin_0, Atmega328.AVCC, U1.VCC
  N14: XTAL1.pin_0, Atmega328.XLAT2
  N15: XTAL1.pin_1, Atmega328.XLAT1
  N16: R10.Pin_1, Atmega328.RESET
  N17: Atmega328.D0_(RX), U1.RO
  N18: Atmega328.D1_(TX), U1.DI
  N19: U1.GND, J3.pin1
  N20: U1.A, J3.pin2
  N21: U1.B, J3.pin3
  N22: Q6.drain, R11.Pin_1, R12.Pin_1, R13.Pin_1
  N23: J2.pin1, R13.Pin_0
  N24: J2.pin2, R12.Pin_0
  N25: J2.pin3, R11.Pin_0
  N26: J2.pin4, R15.Pin_0
  N27: J2.pin5, R16.Pin_0
  N28: J2.pin6, R14.Pin_0
  N29: J2.pin7, R18.Pin_0
  N30: J2.pin8, R19.Pin_0
  N31: J2.pin9, R17.Pin_0
