# Fritzing sketch withArduino (saved by Fritzing 0.9.0b)
circuit board: 6.84003cm x 5.90552cm
breadboards: 1

parts:
  R7 = Resistor [tolerance=±5% resistance=22k package=THT]
  R6 = Resistor [tolerance=±5% resistance=3.3 package=THT]
  R9 = Resistor [tolerance=±5% resistance=3.3 package=THT]
  Q4 = Basic FET N-Channel [package="TO220 [THT]"]
  R4 = Resistor [tolerance=±5% resistance=22k package=THT]
  R2 = Resistor [tolerance=±5% resistance=1 package=THT]
  R5 = Resistor [tolerance=±5% resistance=3.3 package=THT]
  Q5 = NPN-Transistor [package="TO92 [THT]"]
  R1 = Resistor [tolerance=±5% resistance=22k package=THT]
  R8 = Resistor [tolerance=±5% resistance=3.3 package=THT]
  R3 = Resistor [tolerance=±5% resistance=3.3 package=THT]
  Q2 = Basic FET N-Channel [package="TO220 [THT]"]
  Q1 = NPN-Transistor [package="TO92 [THT]"]
  J1 = screw terminal, 2 pins
  XTAL1 = Crystal [frequency="16 Mhz" package=THT]
  R10 = Resistor [tolerance=±5% resistance=10k package=THT]
  Q3 = NPN-Transistor [package="TO92 [THT]"]
  Atmega328 = atmega328 [package=dip]
  U1 = MAX485 [package=dil08]
  J3 = screw terminal, 4 pins
  Q6 = Basic FET N-Channel [package="TO220 [THT]"]
  U2 = Voltage Regulator - 5V [package="TO220 [THT]"]
  C2 = Capacitor Polarized [package=cpol-radial-10uf-25v]
  C3 = Capacitor Polarized [package=cpol-radial-10uf-25v]
  J2 = screw terminal, 4 pins

nets:
  N1: R7.Pin_0, Atmega328.D9_(PWM)
  N2: R7.Pin_1, Q5.E, Q6.gate
  GND: R6.Pin_0, R9.Pin_0, R2.Pin_0, R5.Pin_0, Q5.C, R8.Pin_0, R3.Pin_0, Q1.C, J1.pin1, Q3.C, Atmega328.GND, U1.RE, U1.DE, U2.GND, C2.-, C3.-
  N3: R6.Pin_1, Q4.source, R5.Pin_1, Q3.B
  N4: R9.Pin_1, Q5.B, R8.Pin_1, Q6.source
  N5: Q4.gate, R4.Pin_1, Q3.E
  N6: Q4.drain, J2.pin2
  N7: R4.Pin_0, Atmega328.D10_(PWM)
  N8: R2.Pin_1, R3.Pin_1, Q2.source, Q1.B
  N9: R1.Pin_0, Atmega328.D11_(PWM)
  N10: R1.Pin_1, Q2.gate, Q1.E
  N11: Q2.drain, J2.pin3
  N12: J1.pin2, U2.input_voltage, C2.+, J2.pin4
  N13: XTAL1.pin_0, Atmega328.XLAT2
  N14: XTAL1.pin_1, Atmega328.XLAT1
  N15: R10.Pin_0, Atmega328.AVCC, U1.VCC, U2.output_voltage, C3.+
  N16: R10.Pin_1, Atmega328.RESET
  N17: Atmega328.D0_(RX), U1.RO
  N18: Atmega328.D1_(TX), U1.DI
  N19: U1.GND, J3.pin1
  N20: U1.A, J3.pin2
  N21: U1.B, J3.pin3
  N22: Q6.drain, J2.pin1
